# Fritzing sketch TGII (saved by Fritzing 0.7.4b)
breadboards: 1

parts:
  Arduino1 = Arduino
  LCD1 = LCD screen
  R1 = Resistor [tolerance=±5% resistance=10k package=THT]
  R2 = Resistor [tolerance=±5% resistance=10k package=THT]
  C1 = Ceramic Capacitor [capacitance=100nF package="100 mil [THT, multilayer]"]
  C2 = Ceramic Capacitor [capacitance=100nF package="100 mil [THT, multilayer]"]
  R3 = Resistor [tolerance=±5% resistance=220 package=THT]
  R4 = Resistor [tolerance=±5% resistance=220 package=THT]
  wheel = Reed switch [package=THT]
  cadence = Reed switch [package=THT]
  R5 = Trimmer Potentiometer [maximum_resistance=10kΩ package=THT]
  J1 = Basic Servo
  VCC1 = Battery
  K-- = Pushbutton [package=THT]
  K++ = Pushbutton [package=THT]

nets:
  GND: Arduino1.GND, LCD1.VSS, LCD1.R/W, R1.Pin_0, R2.Pin_0, C1.1, C2.1, wheel.pin_2, cadence.pin_2, R5.leg1
  N1: Arduino1.D12, R1.Pin_1, K--.leg0
  N2: Arduino1.D11, R2.Pin_1, K++.leg0
  N3: Arduino1.D10, LCD1.DB7
  N4: Arduino1.D9, J1.pulse
  N5: Arduino1.D8, LCD1.DB6
  N6: Arduino1.D7, LCD1.RS
  N7: Arduino1.D6, LCD1.E
  N8: Arduino1.D5, LCD1.DB4
  N9: Arduino1.D4, LCD1.DB5
  N10: Arduino1.D3, C1.0, R3.Pin_1, cadence.pin_1
  N11: Arduino1.D2, C2.0, R4.Pin_1, wheel.pin_1
  +5V: Arduino1.+5V, LCD1.VDD, R3.Pin_0, R4.Pin_0, R5.leg2, K--.leg1, K++.leg1
  N12: LCD1.V0, R5.wiper
  N13: J1.gnd, VCC1.-
  N14: J1.vcc, VCC1.+

// code stored in the sketch: principal.pde
/*
 * Main.pde - Main file to control a bicycle derailleur
 * Version 0.1
 *
 * This is file is part of a my final graduation work.
 * This code is intended to be used with an arduino to
 * automatically control gear changes of a commom
 * bicycle derailleur.
 *
 * Variables prefixed with "w" are referenced to wheel
 * Variables prefixed with "c" are referenced to the cadence
 *
 * Author: Paulo S. Machado
 * Date: October 2011
 *
 * Release under de GNU Public License v3.0 or greater
 * This library is free software; you can redistribute it and/or
 * modify it under the terms of the GNU General Public
 * License as published by the Free Software Foundation; either
 * version 3.0 of the License, or (at your option) any later version.
 *
 * This library is distributed in the hope that it will be useful,
 * but WITHOUT ANY WARRANTY; without even the implied warranty of
 * MERCHANTABILITY or FITNESS FOR A PARTICULAR PURPOSE.  See the GNU
 * General Public License for more details.
 *
 * You should have received a copy of the GNU Lesser General Public
 * License along with this library; if not, write to the Free Software
 * Foundation, Inc., 51 Franklin St, Fifth Floor, Boston, MA  02110-1301  USA
 */

#include <LiquidCrystal.h>
#include <BikeTransmission.h>
#include <Servo.h>



// Objects instatiation
Servo motor;
Derailleur trocador;
LiquidCrystal lcd ( 7, 6, 5, 4, 8, 10 );
RearWheel roda ( 0.65 );  

// Constants
const int b0Pin = 11;   // K-
const int b1Pin = 12;   // K+
const int r0Pin = 3;    // Wheel
const int r1Pin = 2;    // Cadence
const int pwmPin = 9;   // PWM pin
const unsigned int CADENCE_MIN = 3000;  // MIN SPEED = MAX TIME coasting
const unsigned long RESET_TIMEOUT = 3000; // Timeout for reset timers
const int debugLevel = 2; // Set debug verbosity in serial

const int TOTAL_GEARS=6;
const int TOLERANCE=5;
const float validratios[TOTAL_GEARS]={1.0769, 1.2174, 1.4, 1.6471, 1.8667, 2.1538};

// Variables
unsigned int wspeed, state=1;
int gear=6;
float K=1.00;

float ratio;

// Interrupt used variables
volatile boolean w=false;
volatile boolean c=false;
volatile unsigned long ctime=0;
volatile unsigned long wtime=0;
volatile unsigned long ctimeLog[2];
volatile unsigned long wtimeLog[2];

/*
 * General pins and startup routine
 */
void setup() {
  Serial.begin ( 9600 );
  lcd.begin ( 16,2 ); 
  lcd.print( "start up..." );
  delay(2000); 
  lcd.clear(); 
  lcd.print ( "Vel:" );
  lcd.setCursor ( 8,0 ); 
  lcd.print ( "kmph" );
  lcd.setCursor ( 0,1 ); 
  lcd.print ( "Marcha:" );
  lcd.setCursor ( 10,1 ); 
  lcd.print ( "K:" );
  motor.attach ( pwmPin );
  pinMode ( b0Pin, INPUT );
  pinMode ( b1Pin, INPUT );
  pinMode ( r0Pin, INPUT );
  pinMode ( r1Pin, INPUT );
  attachInterrupt ( 1, wheel_monitor, FALLING );
  attachInterrupt ( 0, cadence_monitor, FALLING );
}

/*
 * Display refresh routine
 */
void update_lcd() {
  lcd.setCursor ( 4,0 );
  lcd.print("    ");
  lcd.setCursor ( 4,0 );
  lcd.print ( wspeed );
  lcd.setCursor ( 7,1 );
  lcd.print ( gear );
  lcd.setCursor ( 12,1 );
  lcd.print ( K );
}

/*
 * Serial debug output routine
 */
void update_serial() {
  if (debugLevel == 2) {
    Serial.print ( "Velocidade: " );    Serial.print ( wspeed ); Serial.println (" kmph");
    Serial.print ( "Marcha: " );        Serial.println ( gear );
    Serial.print ( "Tempo roda: " );    Serial.print ( wtime ); Serial.println ( " ms" );
    Serial.print ( "Tempo cadencia: " );Serial.print ( ctime ); Serial.println ( " ms" );
    Serial.print ("K: ");               Serial.println (K);     Serial.println ("");
  }
}

/*
 * Main loop
 */
void loop() {
  ratio=float(ctime)/wtime;
  for (int i=0;i<6;i++) {
      if (closeto(ratio,validratios[i],TOLERANCE)) {
          gear = i+1;
      }
  }
  
  // check if coasting
  if (( ctime < CADENCE_MIN ) && ( ctime != 0)) {
    // if not act over transmission
    trocador.set_gear ( motor, gear, ctime, wtime, K );
  }
  /*
   * Refresh displays
   */ 
  wspeed = roda.get_lspeed ( wtime );
  update_lcd();
  update_serial();
  /*
   * Button 1 read, k++
   */
  if ( digitalRead ( b1Pin ) == HIGH ) {
    K=K+0.01;
    if ( K >= 1.5 ) {
      K = 1.5;
    }
  }
  /*
   * Button 0 read, k--
   */
  if ( digitalRead ( b0Pin ) == HIGH ) {
    K=K-0.01;
    if ( K <= 0.5 ) {
      K = 0.5;
    }
  }
  delay ( 600 );
  reset_timers();
}

/*
 * wheel time interrupt
 * routine
 */
void wheel_monitor() {
  // first time log
  if ( w == false ) {
    wtimeLog[0] = millis();
    w=true;
  }
  else {
    wtimeLog[1] = millis();
    wtime = wtimeLog[1] - wtimeLog[0];
    wtimeLog[0] = wtimeLog[1];
  }
}

/*
 * cadence time interrupt
 * routine
 */
void cadence_monitor() {
  // first time log
  if ( c == false ) {
    ctimeLog[0] = millis();
    c=true;
  }
  else {
    ctimeLog[1] = millis();
    ctime = ctimeLog[1] - ctimeLog[0];
    ctimeLog[0] = ctimeLog[1];
  }
}

/*
 * timers reset routine
 */
void reset_timers() {
  unsigned long now = millis();
  if (now - wtimeLog[0] > RESET_TIMEOUT) {
    wtime = 0;
  }
  if (now - ctimeLog[0] > RESET_TIMEOUT) {
    ctime = 0;
  }
}

/*
 * Return true if param is within
 * tolerance [%] of reference:
 */
boolean closeto(float param, float reference, float tolerance) {
    return ( (param >= (reference*(100-tolerance)/100) ) &&
      (param <= (reference*(100+tolerance)/100) ) );
}
